# Fritzing sketch chambre (saved by Fritzing 0.9.3b)

parts:
  Composant1 = Arduino Uno (Rev3)  # not connected
  8_Channel_Relay1 = 8 Channel Power Relay
  Grove1 = Grove Light Sensor
  Grove2 = Grove - Temperature&Humidity Sensor DHT11
  Composant2 = Arduino Ethernet Shield (Rev3)  # not connected
  Composant3 = Base Shield V2
  Grove3 = Grove RGB LCD
  Grove4 = Grove-I2C

nets:
  GND: 8_Channel_Relay1.GND, Composant3.GND
  N1: 8_Channel_Relay1.IN1, Composant3.D4
  N2: 8_Channel_Relay1.IN2, Composant3.D5
  N3: 8_Channel_Relay1.IN3, Composant3.D6_PWM
  N4: 8_Channel_Relay1.IN4, Composant3.D7
  N5: 8_Channel_Relay1.IN5, Composant3.D8
  N6: 8_Channel_Relay1.VCC#17, Composant3.5V
  N7: 8_Channel_Relay1.VCC#19, 8_Channel_Relay1.JD-VCC
  N8: Grove1.GND, Composant3.pin_147
  N9: Grove1.VCC, Composant3.pin_146
  N10: Grove1.SIG, Composant3.pin_144
  N11: Grove2.GND, Composant3.pin_140
  N12: Grove2.VCC, Composant3.pin_141
  N13: Grove2.DIO, Composant3.pin_142
  N14: Grove2.CLK, Composant3.pin_143
  N15: Composant3.pin_132, Grove4.GND
  N16: Composant3.pin_133, Grove4.VCC
  N17: Composant3.pin_134, Grove4.SDA
  N18: Composant3.pin_135, Grove4.SCL
  N19: Composant3.pin_136, Grove3.GND
  N20: Composant3.pin_137, Grove3.VCC
  N21: Composant3.pin_138, Grove3.SDA
  N22: Composant3.pin_139, Grove3.SCL

custom parts:
  8 Channel Power Relay: An 8 channel power relay. The module operates at 5V.
